// Logisim project Clock.circ as structural Verilog: 1 circuit, main circuit main
module main (
  input  _0,
  input  in_2,
  input  in_3,
  input  _1,
  input  _1_2,
  input  in_6,
  input  in_7
);

  wire A_qn, and_1_out, and_2_out, and_3_out, and_4_out, and_5_out, and_6_out, and_7_out, B_2_qn, B_qn,
       clock_1_out, clock_2_out, decoder_1_out0, decoder_1_out1, decoder_1_out2, decoder_1_out3,
       decoder_1_out4, decoder_1_out5, decoder_1_out6, decoder_1_out7, decoder_1_out8, decoder_1_out9,
       decoder_2_out0, decoder_2_out1, decoder_2_out2, decoder_2_out3, decoder_2_out4, decoder_2_out5,
       or_1_out, or_9_out, or_10_out, or_11_out, or_12_out, or_13_out, or_14_out, or_15_out, or_16_out,
       xor_1_out;
  wire [3:0] D_2_q, D_q;
  wire [6:0] or_8_out;

  Clock clock_1 (.out(clock_1_out));
  T_Flip_Flop A (.clk(clock_1_out), .T(or_1_out), .Q(D_q[3]), .Qn(A_qn), .reset(in_7), .en(in_2));  // open: preset
  T_Flip_Flop B (.clk(clock_1_out), .T(and_3_out), .Q(D_q[2]), .Qn(B_qn), .reset(in_7), .en(in_2));  // open: preset
  T_Flip_Flop C (.clk(clock_1_out), .T(and_4_out), .Q(D_q[1]), .reset(in_7), .en(in_2));  // open: Qn, preset
  T_Flip_Flop D (.clk(clock_1_out), .T(_1_2), .Q(D_q[0]), .reset(in_7), .en(in_2));  // open: Qn, preset
  and and_1 (and_1_out, D_q[3], B_qn, D_q[0]);
  and and_2 (and_2_out, D_q[2], D_q[1], D_q[0]);
  and and_3 (and_3_out, D_q[1], D_q[0]);
  and and_4 (and_4_out, A_qn, D_q[0]);
  or or_1 (or_1_out, and_1_out, and_2_out);
  Decoder #(.select(4)) decoder_1 (
    .out0(decoder_1_out0), .out1(decoder_1_out1), .out2(decoder_1_out2), .out3(decoder_1_out3),
    .out4(decoder_1_out4), .out5(decoder_1_out5), .out6(decoder_1_out6), .out7(decoder_1_out7),
    .out8(decoder_1_out8), .out9(decoder_1_out9), .sel(D_q), .en(in_2));  // open: out10, out11, out12, out13, out14, out15
  or or_2 (or_8_out[6], decoder_1_out0, decoder_1_out2, decoder_1_out3, decoder_1_out5, decoder_1_out6, decoder_1_out7, decoder_1_out8, decoder_1_out9);
  or or_3 (or_8_out[5], decoder_1_out0, decoder_1_out1, decoder_1_out2, decoder_1_out3, decoder_1_out4, decoder_1_out7, decoder_1_out8, decoder_1_out9);
  or or_4 (or_8_out[4], decoder_1_out0, decoder_1_out1, decoder_1_out3, decoder_1_out4, decoder_1_out5, decoder_1_out6, decoder_1_out7, decoder_1_out8, decoder_1_out9);
  or or_5 (or_8_out[3], decoder_1_out0, decoder_1_out2, decoder_1_out3, decoder_1_out5, decoder_1_out6, decoder_1_out8, decoder_1_out9);
  or or_6 (or_8_out[2], decoder_1_out0, decoder_1_out2, decoder_1_out6, decoder_1_out8);
  or or_7 (or_8_out[1], decoder_1_out0, decoder_1_out4, decoder_1_out5, decoder_1_out6, decoder_1_out8, decoder_1_out9);
  or or_8 (or_8_out[0], decoder_1_out2, decoder_1_out3, decoder_1_out4, decoder_1_out5, decoder_1_out6, decoder_1_out8, decoder_1_out9);
  and and_5 (and_5_out, decoder_1_out0, decoder_1_out1, decoder_1_out2, decoder_1_out3, decoder_1_out5, decoder_1_out6, decoder_1_out7, decoder_1_out8);
  Clock clock_2 (.out(clock_2_out));
  xor xor_1 (xor_1_out, and_5_out, decoder_1_out9);
  T_Flip_Flop A_2 (.clk(clock_2_out), .T(_0), .Q(D_2_q[3]), .reset(in_6), .en(xor_1_out));  // open: Qn, preset
  T_Flip_Flop B_2 (
    .clk(clock_2_out), .T(and_6_out), .Q(D_2_q[2]), .Qn(B_2_qn), .reset(in_6), .en(xor_1_out));  // open: preset
  T_Flip_Flop C_2 (.clk(clock_2_out), .T(and_7_out), .Q(D_2_q[1]), .reset(in_6), .en(xor_1_out));  // open: Qn, preset
  T_Flip_Flop D_2 (.clk(clock_2_out), .T(_1), .Q(D_2_q[0]), .reset(in_6), .en(xor_1_out));  // open: Qn, preset
  or or_9 (or_9_out, D_2_q[2], D_2_q[1]);
  and and_6 (and_6_out, or_9_out, D_2_q[0]);
  and and_7 (and_7_out, B_2_qn, D_2_q[0]);
  Decoder #(.select(4)) decoder_2 (
    .out0(decoder_2_out0), .out1(decoder_2_out1), .out2(decoder_2_out2), .out3(decoder_2_out3),
    .out4(decoder_2_out4), .out5(decoder_2_out5), .sel(D_2_q), .en(in_3));  // open: out6, out7, out8, out9, out10, out11, out12, out13, out14, out15
  or or_10 (or_10_out, decoder_2_out0, decoder_2_out2, decoder_2_out3, decoder_2_out5);
  or or_11 (or_11_out, decoder_2_out0, decoder_2_out1, decoder_2_out2, decoder_2_out3, decoder_2_out4);
  or or_12 (or_12_out, decoder_2_out0, decoder_2_out1, decoder_2_out3, decoder_2_out4, decoder_2_out5);
  or or_13 (or_13_out, decoder_2_out0, decoder_2_out2, decoder_2_out3, decoder_2_out5);
  or or_14 (or_14_out, decoder_2_out0, decoder_2_out2);
  or or_15 (or_15_out, decoder_2_out0, decoder_2_out4, decoder_2_out5);
  or or_16 (or_16_out, decoder_2_out2, decoder_2_out3, decoder_2_out4, decoder_2_out5);
  _7_Segment_Display u_7_segment_display_1 (
    .g(or_16_out), .f(or_15_out), .a(or_10_out), .b(or_11_out), .e(or_14_out), .d(or_13_out), .c(or_12_out));  // open: dp
  _7_Segment_Display u_7_segment_display_2 (
    .g(or_8_out[0]), .f(or_8_out[1]), .a(or_8_out[6]), .b(or_8_out[5]), .e(or_8_out[2]), .d(or_8_out[3]),
    .c(or_8_out[4]));  // open: dp
endmodule
