// Logisim project Clock1.circ as structural Verilog: 1 circuit, main circuit main
module main (
  input  _0,
  input  in_2,
  input  in_3,
  input  in_4,
  input  in_5,
  input  in_6,
  input  in_7,
  input  _1,
  input  _1_2,
  input  in_10,
  input  in_11,
  input  in_12,
  input  in_13
);

  wire A_3_qn, A_qn, and_1_out, and_2_out, and_3_out, and_4_out, and_5_out, and_6_out, and_7_out, and_8_out,
       and_9_out, and_10_out, and_11_out, and_12_out, and_13_out, and_14_out, and_15_out, B_2_qn, B_qn,
       clock_1_out, clock_2_out, clock_3_out, clock_4_out, decoder_1_out0, decoder_1_out1, decoder_1_out2,
       decoder_1_out3, decoder_1_out4, decoder_1_out5, decoder_1_out6, decoder_1_out7, decoder_1_out8,
       decoder_1_out9, decoder_2_out0, decoder_2_out1, decoder_2_out2, decoder_2_out3, decoder_2_out4,
       decoder_2_out5, decoder_2_out6, decoder_3_out0, decoder_3_out1, decoder_3_out2, decoder_3_out3,
       decoder_3_out4, decoder_3_out5, decoder_3_out6, decoder_3_out7, decoder_3_out8, decoder_3_out9,
       decoder_4_out0, decoder_4_out1, or_1_out, or_9_out, or_17_out, or_18_out, or_19_out, or_27_out,
       or_28_out, xor_1_out, xor_2_out;
  wire [3:0] D_2_q, D_3_q, D_4_q, D_q;
  wire [6:0] or_8_out, or_16_out, or_26_out;

  Clock clock_1 (.out(clock_1_out));
  T_Flip_Flop A (.clk(clock_1_out), .T(or_1_out), .Q(D_q[3]), .Qn(A_qn), .reset(in_13), .en(in_2));  // open: preset
  T_Flip_Flop B (.clk(clock_1_out), .T(and_3_out), .Q(D_q[2]), .Qn(B_qn), .reset(in_13), .en(in_2));  // open: preset
  T_Flip_Flop C (.clk(clock_1_out), .T(and_4_out), .Q(D_q[1]), .reset(in_13), .en(in_2));  // open: Qn, preset
  T_Flip_Flop D (.clk(clock_1_out), .T(_1_2), .Q(D_q[0]), .reset(in_13), .en(in_2));  // open: Qn, preset
  and and_1 (and_1_out, D_q[3], B_qn, D_q[0]);
  and and_2 (and_2_out, D_q[2], D_q[1], D_q[0]);
  and and_3 (and_3_out, D_q[1], D_q[0]);
  and and_4 (and_4_out, A_qn, D_q[0]);
  or or_1 (or_1_out, and_1_out, and_2_out);
  Decoder #(.select(4)) decoder_1 (
    .out0(decoder_1_out0), .out1(decoder_1_out1), .out2(decoder_1_out2), .out3(decoder_1_out3),
    .out4(decoder_1_out4), .out5(decoder_1_out5), .out6(decoder_1_out6), .out7(decoder_1_out7),
    .out8(decoder_1_out8), .out9(decoder_1_out9), .sel(D_q), .en(in_2));  // open: out10, out11, out12, out13, out14, out15
  or or_2 (or_8_out[6], decoder_1_out0, decoder_1_out2, decoder_1_out3, decoder_1_out5, decoder_1_out6, decoder_1_out7, decoder_1_out8, decoder_1_out9);
  or or_3 (or_8_out[5], decoder_1_out0, decoder_1_out1, decoder_1_out2, decoder_1_out3, decoder_1_out4, decoder_1_out7, decoder_1_out8, decoder_1_out9);
  or or_4 (or_8_out[4], decoder_1_out0, decoder_1_out1, decoder_1_out3, decoder_1_out4, decoder_1_out5, decoder_1_out6, decoder_1_out7, decoder_1_out8, decoder_1_out9);
  or or_5 (or_8_out[3], decoder_1_out0, decoder_1_out2, decoder_1_out3, decoder_1_out5, decoder_1_out6, decoder_1_out8, decoder_1_out9);
  or or_6 (or_8_out[2], decoder_1_out0, decoder_1_out2, decoder_1_out6, decoder_1_out8);
  or or_7 (or_8_out[1], decoder_1_out0, decoder_1_out4, decoder_1_out5, decoder_1_out6, decoder_1_out8, decoder_1_out9);
  or or_8 (or_8_out[0], decoder_1_out2, decoder_1_out3, decoder_1_out4, decoder_1_out5, decoder_1_out6, decoder_1_out8, decoder_1_out9);
  and and_5 (and_5_out, decoder_1_out0, decoder_1_out1, decoder_1_out2, decoder_1_out3, decoder_1_out5, decoder_1_out6, decoder_1_out7, decoder_1_out8);
  Clock clock_2 (.out(clock_2_out));
  xor xor_1 (xor_1_out, and_5_out, decoder_1_out9);
  T_Flip_Flop A_2 (.clk(clock_2_out), .T(_0), .Q(D_2_q[3]), .reset(in_12), .en(xor_1_out));  // open: Qn, preset
  T_Flip_Flop B_2 (
    .clk(clock_2_out), .T(and_6_out), .Q(D_2_q[2]), .Qn(B_2_qn), .reset(in_12), .en(xor_1_out));  // open: preset
  T_Flip_Flop C_2 (.clk(clock_2_out), .T(and_7_out), .Q(D_2_q[1]), .reset(in_12), .en(xor_1_out));  // open: Qn, preset
  T_Flip_Flop D_2 (.clk(clock_2_out), .T(_1), .Q(D_2_q[0]), .reset(in_12), .en(xor_1_out));  // open: Qn, preset
  or or_9 (or_9_out, D_2_q[2], D_2_q[1]);
  and and_6 (and_6_out, or_9_out, D_2_q[0]);
  and and_7 (and_7_out, B_2_qn, D_2_q[0]);
  Decoder #(.select(4)) decoder_2 (
    .out0(decoder_2_out0), .out1(decoder_2_out1), .out2(decoder_2_out2), .out3(decoder_2_out3),
    .out4(decoder_2_out4), .out5(decoder_2_out5), .out6(decoder_2_out6), .sel(D_2_q), .en(in_3));  // open: out7, out8, out9, out10, out11, out12, out13, out14, out15
  or or_10 (or_16_out[6], decoder_2_out0, decoder_2_out2, decoder_2_out3, decoder_2_out5);
  or or_11 (or_16_out[5], decoder_2_out0, decoder_2_out1, decoder_2_out2, decoder_2_out3, decoder_2_out4);
  or or_12 (or_16_out[4], decoder_2_out0, decoder_2_out1, decoder_2_out3, decoder_2_out4, decoder_2_out5);
  or or_13 (or_16_out[3], decoder_2_out0, decoder_2_out2, decoder_2_out3, decoder_2_out5);
  or or_14 (or_16_out[2], decoder_2_out0, decoder_2_out2);
  or or_15 (or_16_out[1], decoder_2_out0, decoder_2_out4, decoder_2_out5);
  or or_16 (or_16_out[0], decoder_2_out2, decoder_2_out3, decoder_2_out4, decoder_2_out5);
  and and_8 (and_8_out, decoder_2_out5, xor_1_out);
  Clock clock_3 (.out(clock_3_out));
  T_Flip_Flop A_3 (
    .clk(clock_3_out), .T(or_18_out), .Q(D_3_q[3]), .Qn(A_3_qn), .reset(in_10), .en(and_8_out));  // open: preset
  T_Flip_Flop B_3 (.clk(clock_3_out), .T(and_10_out), .Q(D_3_q[2]), .reset(in_10), .en(and_8_out));  // open: Qn, preset
  T_Flip_Flop C_3 (.clk(clock_3_out), .T(or_19_out), .Q(D_3_q[1]), .reset(in_10), .en(and_8_out));  // open: Qn, preset
  T_Flip_Flop D_3 (.clk(clock_3_out), .T(in_6), .Q(D_3_q[0]), .reset(in_10), .en(and_8_out));  // open: Qn, preset
  or or_17 (or_17_out, D_3_q[1], D_3_q[0]);
  and and_9 (and_9_out, D_3_q[2], D_3_q[1], D_3_q[0]);
  and and_10 (and_10_out, D_3_q[1], D_3_q[0]);
  and and_11 (and_11_out, A_3_qn, D_3_q[0]);
  and and_12 (and_12_out, D_3_q[3], D_3_q[1]);
  and and_13 (and_13_out, D_3_q[3], or_17_out);
  or or_18 (or_18_out, and_13_out, and_9_out);
  or or_19 (or_19_out, and_11_out, and_12_out);
  Decoder #(.select(4)) decoder_3 (
    .out0(decoder_3_out0), .out1(decoder_3_out1), .out2(decoder_3_out2), .out3(decoder_3_out3),
    .out4(decoder_3_out4), .out5(decoder_3_out5), .out6(decoder_3_out6), .out7(decoder_3_out7),
    .out8(decoder_3_out8), .out9(decoder_3_out9), .sel(D_3_q), .en(in_4));  // open: out10, out11, out12, out13, out14, out15
  or or_20 (or_26_out[6], decoder_3_out0, decoder_3_out2, decoder_3_out3, decoder_3_out5, decoder_3_out6, decoder_3_out7, decoder_3_out8, decoder_3_out9);
  or or_21 (or_26_out[5], decoder_3_out0, decoder_3_out1, decoder_3_out2, decoder_3_out3, decoder_3_out4, decoder_3_out7, decoder_3_out8, decoder_3_out9);
  or or_22 (or_26_out[4], decoder_3_out0, decoder_3_out1, decoder_3_out3, decoder_3_out4, decoder_3_out5, decoder_3_out6, decoder_3_out7, decoder_3_out8, decoder_3_out9);
  or or_23 (or_26_out[3], decoder_3_out0, decoder_3_out2, decoder_3_out3, decoder_3_out5, decoder_3_out6, decoder_3_out8, decoder_3_out9);
  or or_24 (or_26_out[2], decoder_3_out0, decoder_3_out2, decoder_3_out6, decoder_3_out8);
  or or_25 (or_26_out[1], decoder_3_out0, decoder_3_out4, decoder_3_out5, decoder_3_out6, decoder_3_out8, decoder_3_out9);
  or or_26 (or_26_out[0], decoder_3_out2, decoder_3_out3, decoder_3_out4, decoder_3_out5, decoder_3_out6, decoder_3_out8, decoder_3_out9);
  and and_14 (and_14_out, decoder_3_out9, and_8_out);
  and and_15 (and_15_out, decoder_3_out2, decoder_4_out1);
  xor xor_2 (xor_2_out, and_14_out, and_15_out);
  Clock clock_4 (.out(clock_4_out));
  T_Flip_Flop A_4 (.clk(clock_4_out), .Q(D_4_q[3]), .reset(in_11), .en(xor_2_out));  // open: T, Qn, preset
  T_Flip_Flop B_4 (.clk(clock_4_out), .Q(D_4_q[2]), .reset(in_11), .en(xor_2_out));  // open: T, Qn, preset
  T_Flip_Flop C_4 (.clk(clock_4_out), .Q(D_4_q[1]), .reset(in_11), .en(xor_2_out));  // open: T, Qn, preset
  T_Flip_Flop D_4 (.clk(clock_4_out), .T(in_7), .Q(D_4_q[0]), .reset(in_11), .en(xor_2_out));  // open: Qn, preset
  Decoder #(.select(4)) decoder_4 (
    .out0(decoder_4_out0), .out1(decoder_4_out1), .sel(D_4_q), .en(in_5));  // open: out2, out3, out4, out5, out6, out7, out8, out9, out10, out11, out12, out13, out14, out15
  or or_27 (or_27_out, decoder_4_out0, decoder_4_out1);
  or or_28 (or_28_out, decoder_4_out0, decoder_4_out1);
  _7_Segment_Display u_7_segment_display_1 (
    .f(decoder_4_out0), .a(decoder_4_out0), .b(or_27_out), .e(decoder_4_out0), .d(decoder_4_out0),
    .c(or_28_out));  // open: g, dp
  _7_Segment_Display u_7_segment_display_2 (
    .g(or_26_out[0]), .f(or_26_out[1]), .a(or_26_out[6]), .b(or_26_out[5]), .e(or_26_out[2]),
    .d(or_26_out[3]), .c(or_26_out[4]), .dp(in_6));
  _7_Segment_Display u_7_segment_display_3 (
    .g(or_16_out[0]), .f(or_16_out[1]), .a(or_16_out[6]), .b(or_16_out[5]), .e(or_16_out[2]),
    .d(or_16_out[3]), .c(or_16_out[4]));  // open: dp
  _7_Segment_Display u_7_segment_display_4 (
    .g(or_8_out[0]), .f(or_8_out[1]), .a(or_8_out[6]), .b(or_8_out[5]), .e(or_8_out[2]), .d(or_8_out[3]),
    .c(or_8_out[4]));  // open: dp
endmodule
